# Fritzing sketch Plant Monitor (saved by Fritzing 0.9.3b)
breadboards: 1

parts:
  U1 = NodeMCU V1.0
  DHT1 = DHT22 Humidity and Temperature Sensor
  JACK1 = 2.1mm DC Barrel Jack
  R1 = Resistor [tolerance=±5% resistance=10k package="0603 [SMD]"]
  Soil = mystery part, 4 pins [chip_label=Soil]  # not connected
  ADC1 = MCP3008 [package=dil16]
  U2 = Vibration Motor- ROB-08449 [package=vibe-motor-10mm]
  Q1 = MOSFET-NCHANNEL [package=to220v]
  R2 = Resistor [tolerance=±5% resistance=10k package="0603 [SMD]"]
  S1 = SPST Switch [package=switch-spdt_lock.007s]
  DS1 = DS18B20 1-Wire Temperature Sensor [part_number=DS18B20]
  R3 = Resistor [tolerance=±5% resistance=4.7k package="0603 [SMD]"]
  Part1 = Adafruit TSL2591 [part_number="Adafruit #1980"]
  R4 = Resistor [tolerance=±5% resistance=4.7k package="0603 [SMD]"]
  R5 = Resistor [tolerance=±5% resistance=4.7k package="0603 [SMD]"]
  D1 = Diode [package=diode-1n4001]
  U3 = Voltage Regulator - 5V [package="DPak [SMD]"]
  C1 = Ceramic Capacitor [capacitance=100nF package="200 mil [THT, multilayer]"]
  C3 = Electrolytic Capacitor [capacitance=100µF voltage=50V package="200 mil [THT, electrolytic]"]
  C4 = Electrolytic Capacitor [capacitance=10µF package="100 mil [THT, electrolytic]"]
  C5 = Ceramic Capacitor [capacitance=100nF package="200 mil [THT, multilayer]"]

nets:
  N1: U1.D1, Part1.SCL, R4.Pin_0
  N2: U1.D2, Part1.SDA, R5.Pin_0
  N3: U1.D3, DS1.DQ, R3.Pin_0
  N4: U1.D4, Q1.G, R2.Pin_0
  VDD: U1.3V3, DHT1.VDD, R1.Pin_1, ADC1.VREF, ADC1.VDD, DS1.VDD, R3.Pin_1, Part1.VIN, R4.Pin_1, R5.Pin_1, C5.0
  GND: U1.GND, DHT1.GND, JACK1.switch, ADC1.DGND, ADC1.AGND, Q1.S, R2.Pin_1, DS1.GND, Part1.GND, U3.GND, C1.1, C3.-, C4.-, C5.1
  N5: U1.D5, ADC1.CLK
  N6: U1.D6, ADC1.Dout
  N7: U1.D7, ADC1.Din
  N8: U1.D8, ADC1.CS/SHDN
  N9: U1.Vin, U3.output_voltage, C1.0, C4.+
  N10: U1.SD3, DHT1.DATA, R1.Pin_0
  N11: JACK1.center, S1.P, U3.input_voltage, C3.+
  N12: U2.+, Q1.D, D1.A
  N13: U2.-, S1.S, D1.C

notes:
  5V
  3V3
  Blue wires = 12V
  12V DC Input

custom parts:
  NodeMCU V1.0: ESP8266 based NodeMCU
  2.1mm DC Barrel Jack: 2.1mm DC Barrel Jack with Thru-Hole Connectors (breadboardable)
  Adafruit TSL2591: When the future is dazzlingly-bright, this ultra-high-range luminosity sensor will help you measure it. The TSL2591 luminosity sensor is an advanced digital light sensor, ideal for use in a wide range of light situations. Compared to low cost CdS cells, this sensor is more precise, allowing for exact lux calculations and can be configured for different gain/timing ranges to detect light ranges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
